# Fritzing sketch schema_electrica (saved by Fritzing 0.9.3b)

parts:
  Parte1 = Arduino Uno (Rev3)
  Display1 = LCD screen 16x2 IIC [part_number=101290]
  Parte3 = RFID-RC522-v2
  Keypad4x1 = Keypad Membran 4x4
  J2 = Basic Servo
  Part1 = Passive Buzzer

nets:
  N1: Parte1.A0, Keypad4x1.Pin1
  N2: Parte1.A1, Keypad4x1.Pin2
  N3: Parte1.A2, Keypad4x1.Pin3
  N4: Parte1.A3, Keypad4x1.Pin4
  N5: Parte1.A4/SDA, Display1.SDA
  N6: Parte1.A5/SCL, Display1.SCL
  N7: Parte1.D9_PWM, Parte3.RST
  N8: Parte1.D10_PWM/SS, Parte3.SDA
  N9: Parte1.D11_PWM/MOSI, Parte3.MOSI
  N10: Parte1.D12/MISO, Parte3.MISO
  N11: Parte1.D13/SCK, Parte3.SCK
  GND: Parte1.GND, Display1.GND, Parte3.GND, J2.gnd, Part1.GND
  N12: Parte1.D1/TX, Keypad4x1.Pin8
  N13: Parte1.D2, Keypad4x1.Pin7
  N14: Parte1.D3_PWM, Keypad4x1.Pin6
  N15: Parte1.D4, Keypad4x1.Pin5
  N16: Parte1.D5_PWM, Part1.NC
  N17: Parte1.D6_PWM, J2.pulse
  3V3: Parte1.3V3, Parte3.3.3V
  VCC: Parte1.5V, Display1.VCC, J2.vcc, Part1.S

custom parts:
  LCD screen 16x2 IIC: LCD screen with HD44780 controller enables showing text, symbols, value or anything else that comes from Croduino/Arduino. It is capable of showing 16 symbols in two lines and therefore can be used in many projects that need to send clearly visible and legible output information.. • Color of symbols: White • Backlight: Blue • Dimensions: 80 x 36 x 12 mm • Screen dimensions: 64.5 x 16 mm •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
  RFID-RC522-v2: A simple China made RFID-RC522 Reader; do check the pin labels, as this is a MFRC522 based clone.
  Keypad Membran 4x4: Membrane Keypad 4x4 Matrix
